# Fritzing sketch led (saved by Fritzing 1.0.5)
breadboards: 1

parts:
  Part1 = LED Matrix - Serial Interface - Red/Green/Blue
  Part2 = Arduino Uno (Rev3)

nets:
  VCC: Part1.VCC, Part2.5V
  N1: Part1.SCK, Part2.D5_PWM
  N2: Part1.CS, Part2.D4
  N3: Part1.MISO, Part2.D2
  GND: Part1.GND, Part2.GND
  N4: Part1.MOSI, Part2.D3_PWM
